# Fritzing sketch splashback_breadboard_v1 (saved by Fritzing 0.9.3b)
breadboards: 1

parts:
  Part1 = Arduino Uno (Rev3)
  S1 = Reed switch [package=THT]
  S2 = Reed switch [package=THT]
  R1 = Photocell (LDR) [package=THT]
  R2 = Resistor [tolerance=±5% resistance=10k package=THT]
  R3 = Resistor [tolerance=±5% resistance=10k package=THT]
  R4 = Resistor [tolerance=±5% resistance=100k package=THT]
  U1 = ESP8266 WiFi Module [part_number=ESP8266]

nets:
  N1: Part1.A0, R1.pin_1, R4.Pin_0
  N2: Part1.D2, S2.pin_1, R2.Pin_0
  N3: Part1.D3_PWM, S1.pin_1, R3.Pin_0
  N4: Part1.D6_PWM, U1.TX
  N5: Part1.D7, U1.RX
  5V: Part1.5V, S1.pin_2, S2.pin_2, R1.pin_0, U1.3.3V
  N6: Part1.GND, R2.Pin_1, R3.Pin_1, R4.Pin_1
